# Fritzing sketch arduino_aio_sensor (saved by Fritzing 1.0.5)
breadboards: 1

parts:
  Part1 = Arduino Uno (Rev3)
  U1 = mystery part, 4 pins [chip_label="Clap Sensor"]
  IC1 = IC, DIP package, 8 pins [chip_label="4-3 Trans"]
  RHT1 = Humidity and Temperature Sensor RHT03
  Part2 = Bluetooth HC-05 Macho
  U3 = mystery part, 3 pins [chip_label=Touch]
  M1 = fc-51 [package=THT]
  IR1 = TSOP312.., 314.. [package=THT]
  U4 = mystery part, 5 pins [chip_label=Lafvin]
  X1 = USB Connectors [package=usb-a-h]

nets:
  N1: Part1.D8, U3.pin1
  N2: Part1.D10_PWM/SS, Part2.TXD
  N3: Part1.D11_PWM/MOSI, Part2.RXD
  N4: Part1.D12/MISO, IR1.Data
  GND: Part1.GND, U1.pin3, IC1.pin7, IC1.pin8, Part2.GND, U3.pin3, M1.pin2, IR1.GND, U4.pin5, X1.GND
  N5: Part1.D0/RX, X1.D+
  N6: Part1.D1/TX, X1.D-
  N7: Part1.D2, U1.pin4
  N8: Part1.D3_PWM, M1.pin1
  N9: Part1.D4, IC1.pin6
  N10: Part1.D5_PWM, U4.pin3
  N11: Part1.D6_PWM, U4.pin2
  N12: Part1.D7, U4.pin1
  5V: Part1.5V, U1.pin2, IC1.pin5, Part2.VCC, U3.pin2, M1.pin3, IR1.Vs, U4.pin4
  N13: IC1.pin1, RHT1.GND_2
  N14: IC1.pin2, RHT1.GND_1
  N15: IC1.pin3, RHT1.Data-signal
  N16: IC1.pin4, RHT1.Vcc
